// Logisim project DataMemory.circ as structural Verilog: 2 circuits, main circuit main
module main (
  input  [7:0] in_1,
  input  [7:0] write,
  input  [3:0] rs,
  input  regW,
  input  [7:0] in_5,
  input  [3:0] rd,
  input  [3:0] rt
);

  wire clock_1_out, decoder_1_out0, decoder_1_out1, decoder_1_out2, decoder_1_out3, decoder_1_out4,
       decoder_1_out5;
  wire [7:0] multiplexer_1_out, multiplexer_2_out, register_1_q, register_2_q, register_3_q, register_4_q,
       register_5_q, register_6_q, register_7_q;

  Decoder #(.select(3), .disabled(0)) decoder_1 (
    .out0(decoder_1_out0), .out1(decoder_1_out1), .out2(decoder_1_out2), .out3(decoder_1_out3),
    .out4(decoder_1_out4), .out5(decoder_1_out5), .sel(rd[2:0]), .en(regW));  // open: out6, out7
  Clock clock_1 (.out(clock_1_out));
  Register register_1 (.D(write), .Q(register_1_q), .clk(clock_1_out));  // open: en, clr
  Register register_2 (.D(write), .en(decoder_1_out0), .Q(register_2_q), .clk(clock_1_out));  // open: clr
  Register register_3 (.D(write), .en(decoder_1_out1), .Q(register_3_q), .clk(clock_1_out));  // open: clr
  Register register_4 (.D(write), .en(decoder_1_out2), .Q(register_4_q), .clk(clock_1_out));  // open: clr
  Register register_5 (.D(write), .en(decoder_1_out3), .Q(register_5_q), .clk(clock_1_out));  // open: clr
  Register register_6 (.D(write), .en(decoder_1_out4), .Q(register_6_q), .clk(clock_1_out));  // open: clr
  Register register_7 (.D(write), .en(decoder_1_out5), .Q(register_7_q), .clk(clock_1_out));  // open: clr
  Multiplexer #(.select(3), .width(8), .disabled(0)) multiplexer_1 (
    .in0(register_1_q), .in1(register_2_q), .in2(register_3_q), .in3(register_4_q), .in4(register_5_q),
    .in5(register_6_q), .in6(register_7_q), .out(multiplexer_1_out), .sel(rs[2:0]));  // open: in7, en
  Multiplexer #(.select(3), .width(8), .disabled(0)) multiplexer_2 (
    .in0(register_1_q), .in1(register_2_q), .in2(register_3_q), .in3(register_4_q), .in4(register_5_q),
    .in5(register_6_q), .in6(register_7_q), .out(multiplexer_2_out), .sel(rt[2:0]));  // open: in7, en
endmodule

module memory (
  input  [7:0] Address,
  input  [7:0] Data,
  input  [7:0] in_3,
  input  MemWrite,
  input  MemRead,
  input  sp
);

  wire not_1_out;
  wire [7:0] multiplexer_1_out, ram_1_data, ram_2_data;

  not not_1 (not_1_out, sp);
  RAM #(.bus("separate")) ram_1 (
    .addr(Address), .din(Data), .data(ram_1_data), .str(MemWrite), .sel(not_1_out), .ld(MemRead));  // open: clk, clr
  RAM #(.bus("separate")) ram_2 (
    .addr(Address), .din(Data), .data(ram_2_data), .str(MemWrite), .sel(sp), .ld(MemRead));  // open: clk, clr
  Multiplexer #(.width(8), .disabled(0)) multiplexer_1 (
    .in0(ram_1_data), .in1(ram_2_data), .out(multiplexer_1_out), .sel(not_1_out));  // open: en
endmodule
